// Logisim project ALU32.circ as structural Verilog: 5 circuits, main circuit ALU1
module ALU1 (
  input  Ainvert,
  input  A,
  input  B,
  input  Less,
  input  Cin,
  input  Binvert,
  input  [1:0] Operation,
  output Result,
  output Cout
);

  wire and_1_out, fulladder_1_s, multiplexer_1_out, multiplexer_2_out, not_1_out, not_2_out, or_1_out;

  not not_1 (not_1_out, A);
  not not_2 (not_2_out, B);
  Multiplexer multiplexer_1 (.in0(A), .in1(not_1_out), .out(multiplexer_1_out), .sel(Ainvert));
  Multiplexer multiplexer_2 (.in0(B), .in1(not_2_out), .out(multiplexer_2_out), .sel(Binvert));
  and and_1 (and_1_out, multiplexer_1_out, multiplexer_2_out);
  or or_1 (or_1_out, multiplexer_1_out, multiplexer_2_out);
  FullAdder fulladder_1 (.A(multiplexer_1_out), .B(multiplexer_2_out), .Cin(Cin), .S(fulladder_1_s), .Cout(Cout));
  Multiplexer #(.select(2)) multiplexer_3 (
    .in0(and_1_out), .in1(or_1_out), .in2(fulladder_1_s), .in3(Less), .out(Result), .sel(Operation));
endmodule

module FullAdder (
  input  A,
  input  B,
  input  Cin,
  output S,
  output Cout
);

  wire and_1_out, and_2_out, or_1_out, xor_1_out;

  xor xor_1 (xor_1_out, A, B);
  and and_1 (and_1_out, B, A);
  or or_1 (or_1_out, B, A);
  xor xor_2 (S, xor_1_out, Cin);
  and and_2 (and_2_out, or_1_out, Cin);
  or or_2 (Cout, and_1_out, and_2_out);
endmodule

module ALU32bits (
  input  [31:0] B,
  input  [31:0] A,
  input  [3:0] ALUOperation,
  output ZERO,
  output [31:0] out_5
);

  wire alu1_1_cout, alu1_2_cout, alu1_3_cout, alu1_4_cout, alu1_5_cout, alu1_6_cout, alu1_7_cout,
       alu1_8_cout, alu1_9_cout, alu1_10_cout, alu1_11_cout, alu1_12_cout, alu1_13_cout, alu1_14_cout,
       alu1_15_cout, alu1_16_cout, alu1_17_cout, alu1_18_cout, alu1_19_cout, alu1_20_cout, alu1_21_cout,
       alu1_22_cout, alu1_23_cout, alu1_24_cout, alu1_25_cout, alu1_26_cout, alu1_27_cout, alu1_28_cout,
       alu1_29_cout, alu1_30_cout, alu1_31_cout, alu1msb_1_set, or_1_out;

  ALU1 alu1_1 (
    .Ainvert(ALUOperation[3]), .A(A[0]), .B(B[0]), .Less(alu1msb_1_set), .Cin(ALUOperation[2]),
    .Binvert(ALUOperation[2]), .Operation(ALUOperation[1:0]), .Result(out_5[0]), .Cout(alu1_1_cout));
  ALU1 alu1_2 (
    .Ainvert(ALUOperation[3]), .A(A[1]), .B(B[1]), .Less(1'b0), .Cin(alu1_1_cout), .Binvert(ALUOperation[2]),
    .Operation(ALUOperation[1:0]), .Result(out_5[1]), .Cout(alu1_2_cout));
  ALU1 alu1_3 (
    .Ainvert(ALUOperation[3]), .A(A[2]), .B(B[2]), .Less(1'b0), .Cin(alu1_2_cout), .Binvert(ALUOperation[2]),
    .Operation(ALUOperation[1:0]), .Result(out_5[2]), .Cout(alu1_3_cout));
  ALU1 alu1_4 (
    .Ainvert(ALUOperation[3]), .A(A[3]), .B(B[3]), .Less(1'b0), .Cin(alu1_3_cout), .Binvert(ALUOperation[2]),
    .Operation(ALUOperation[1:0]), .Result(out_5[3]), .Cout(alu1_4_cout));
  ALU1 alu1_5 (
    .Ainvert(ALUOperation[3]), .A(A[4]), .B(B[4]), .Less(1'b0), .Cin(alu1_4_cout), .Binvert(ALUOperation[2]),
    .Operation(ALUOperation[1:0]), .Result(out_5[4]), .Cout(alu1_5_cout));
  ALU1 alu1_6 (
    .Ainvert(ALUOperation[3]), .A(A[5]), .B(B[5]), .Less(1'b0), .Cin(alu1_5_cout), .Binvert(ALUOperation[2]),
    .Operation(ALUOperation[1:0]), .Result(out_5[5]), .Cout(alu1_6_cout));
  ALU1 alu1_7 (
    .Ainvert(ALUOperation[3]), .A(A[6]), .B(B[6]), .Less(1'b0), .Cin(alu1_6_cout), .Binvert(ALUOperation[2]),
    .Operation(ALUOperation[1:0]), .Result(out_5[6]), .Cout(alu1_7_cout));
  ALU1 alu1_8 (
    .Ainvert(ALUOperation[3]), .A(A[7]), .B(B[7]), .Less(1'b0), .Cin(alu1_7_cout), .Binvert(ALUOperation[2]),
    .Operation(ALUOperation[1:0]), .Result(out_5[7]), .Cout(alu1_8_cout));
  ALU1 alu1_9 (
    .Ainvert(ALUOperation[3]), .A(A[8]), .B(B[8]), .Less(1'b0), .Cin(alu1_8_cout), .Binvert(ALUOperation[2]),
    .Operation(ALUOperation[1:0]), .Result(out_5[8]), .Cout(alu1_9_cout));
  ALU1 alu1_10 (
    .Ainvert(ALUOperation[3]), .A(A[9]), .B(B[9]), .Less(1'b0), .Cin(alu1_9_cout), .Binvert(ALUOperation[2]),
    .Operation(ALUOperation[1:0]), .Result(out_5[9]), .Cout(alu1_10_cout));
  ALU1 alu1_11 (
    .Ainvert(ALUOperation[3]), .A(A[10]), .B(B[10]), .Less(1'b0), .Cin(alu1_10_cout),
    .Binvert(ALUOperation[2]), .Operation(ALUOperation[1:0]), .Result(out_5[10]), .Cout(alu1_11_cout));
  ALU1 alu1_12 (
    .Ainvert(ALUOperation[3]), .A(A[11]), .B(B[11]), .Less(1'b0), .Cin(alu1_11_cout),
    .Binvert(ALUOperation[2]), .Operation(ALUOperation[1:0]), .Result(out_5[11]), .Cout(alu1_12_cout));
  ALU1 alu1_13 (
    .Ainvert(ALUOperation[3]), .A(A[12]), .B(B[12]), .Less(1'b0), .Cin(alu1_12_cout),
    .Binvert(ALUOperation[2]), .Operation(ALUOperation[1:0]), .Result(out_5[12]), .Cout(alu1_13_cout));
  ALU1 alu1_14 (
    .Ainvert(ALUOperation[3]), .A(A[13]), .B(B[13]), .Less(1'b0), .Cin(alu1_13_cout),
    .Binvert(ALUOperation[2]), .Operation(ALUOperation[1:0]), .Result(out_5[13]), .Cout(alu1_14_cout));
  ALU1 alu1_15 (
    .Ainvert(ALUOperation[3]), .A(A[14]), .B(B[14]), .Less(1'b0), .Cin(alu1_14_cout),
    .Binvert(ALUOperation[2]), .Operation(ALUOperation[1:0]), .Result(out_5[14]), .Cout(alu1_15_cout));
  ALU1 alu1_16 (
    .Ainvert(ALUOperation[3]), .A(A[15]), .B(B[15]), .Less(1'b0), .Cin(alu1_15_cout),
    .Binvert(ALUOperation[2]), .Operation(ALUOperation[1:0]), .Result(out_5[15]), .Cout(alu1_16_cout));
  ALU1 alu1_17 (
    .Ainvert(ALUOperation[3]), .A(A[16]), .B(B[16]), .Less(1'b0), .Cin(alu1_16_cout),
    .Binvert(ALUOperation[2]), .Operation(ALUOperation[1:0]), .Result(out_5[16]), .Cout(alu1_17_cout));
  ALU1 alu1_18 (
    .Ainvert(ALUOperation[3]), .A(A[17]), .B(B[17]), .Less(1'b0), .Cin(alu1_17_cout),
    .Binvert(ALUOperation[2]), .Operation(ALUOperation[1:0]), .Result(out_5[17]), .Cout(alu1_18_cout));
  ALU1 alu1_19 (
    .Ainvert(ALUOperation[3]), .A(A[18]), .B(B[18]), .Less(1'b0), .Cin(alu1_18_cout),
    .Binvert(ALUOperation[2]), .Operation(ALUOperation[1:0]), .Result(out_5[18]), .Cout(alu1_19_cout));
  ALU1 alu1_20 (
    .Ainvert(ALUOperation[3]), .A(A[19]), .B(B[19]), .Less(1'b0), .Cin(alu1_19_cout),
    .Binvert(ALUOperation[2]), .Operation(ALUOperation[1:0]), .Result(out_5[19]), .Cout(alu1_20_cout));
  ALU1 alu1_21 (
    .Ainvert(ALUOperation[3]), .A(A[20]), .B(B[20]), .Less(1'b0), .Cin(alu1_20_cout),
    .Binvert(ALUOperation[2]), .Operation(ALUOperation[1:0]), .Result(out_5[20]), .Cout(alu1_21_cout));
  ALU1 alu1_22 (
    .Ainvert(ALUOperation[3]), .A(A[21]), .B(B[21]), .Less(1'b0), .Cin(alu1_21_cout),
    .Binvert(ALUOperation[2]), .Operation(ALUOperation[1:0]), .Result(out_5[21]), .Cout(alu1_22_cout));
  ALU1 alu1_23 (
    .Ainvert(ALUOperation[3]), .A(A[22]), .B(B[22]), .Less(1'b0), .Cin(alu1_22_cout),
    .Binvert(ALUOperation[2]), .Operation(ALUOperation[1:0]), .Result(out_5[22]), .Cout(alu1_23_cout));
  ALU1 alu1_24 (
    .Ainvert(ALUOperation[3]), .A(A[23]), .B(B[23]), .Less(1'b0), .Cin(alu1_23_cout),
    .Binvert(ALUOperation[2]), .Operation(ALUOperation[1:0]), .Result(out_5[23]), .Cout(alu1_24_cout));
  ALU1 alu1_25 (
    .Ainvert(ALUOperation[3]), .A(A[24]), .B(B[24]), .Less(1'b0), .Cin(alu1_24_cout),
    .Binvert(ALUOperation[2]), .Operation(ALUOperation[1:0]), .Result(out_5[24]), .Cout(alu1_25_cout));
  ALU1 alu1_26 (
    .Ainvert(ALUOperation[3]), .A(A[25]), .B(B[25]), .Less(1'b0), .Cin(alu1_25_cout),
    .Binvert(ALUOperation[2]), .Operation(ALUOperation[1:0]), .Result(out_5[25]), .Cout(alu1_26_cout));
  ALU1 alu1_27 (
    .Ainvert(ALUOperation[3]), .A(A[26]), .B(B[26]), .Less(1'b0), .Cin(alu1_26_cout),
    .Binvert(ALUOperation[2]), .Operation(ALUOperation[1:0]), .Result(out_5[26]), .Cout(alu1_27_cout));
  ALU1 alu1_28 (
    .Ainvert(ALUOperation[3]), .A(A[27]), .B(B[27]), .Less(1'b0), .Cin(alu1_27_cout),
    .Binvert(ALUOperation[2]), .Operation(ALUOperation[1:0]), .Result(out_5[27]), .Cout(alu1_28_cout));
  ALU1 alu1_29 (
    .Ainvert(ALUOperation[3]), .A(A[28]), .B(B[28]), .Less(1'b0), .Cin(alu1_28_cout),
    .Binvert(ALUOperation[2]), .Operation(ALUOperation[1:0]), .Result(out_5[28]), .Cout(alu1_29_cout));
  ALU1 alu1_30 (
    .Ainvert(ALUOperation[3]), .A(A[29]), .B(B[29]), .Less(1'b0), .Cin(alu1_29_cout),
    .Binvert(ALUOperation[2]), .Operation(ALUOperation[1:0]), .Result(out_5[29]), .Cout(alu1_30_cout));
  ALU1 alu1_31 (
    .Ainvert(ALUOperation[3]), .A(A[30]), .B(B[30]), .Less(1'b0), .Cin(alu1_30_cout),
    .Binvert(ALUOperation[2]), .Operation(ALUOperation[1:0]), .Result(out_5[30]), .Cout(alu1_31_cout));
  ALU1MSB alu1msb_1 (
    .Ainvert(ALUOperation[3]), .A(A[31]), .B(B[31]), .Less(1'b0), .Binvert(ALUOperation[2]),
    .Cin(alu1_31_cout), .Operation(ALUOperation[1:0]), .Result(out_5[31]), .Set(alu1msb_1_set));  // open: Cout
  or or_1 (or_1_out, out_5[0], out_5[1], out_5[2], out_5[3], out_5[4], out_5[5], out_5[6], out_5[7], out_5[8], out_5[9], out_5[10], out_5[11], out_5[12], out_5[13], out_5[14], out_5[15], out_5[16], out_5[17], out_5[18], out_5[19], out_5[20], out_5[21], out_5[22], out_5[23], out_5[24], out_5[25], out_5[26], out_5[27], out_5[28], out_5[29], out_5[30], out_5[31]);
  not not_1 (ZERO, or_1_out);

  // Other names for the same wires on the sheet: A00 = A[0]; A01 = A[1]; A02 = A[2]; A03 = A[3]; A04 = A[4];
  //   A05 = A[5]; A06 = A[6]; A07 = A[7]; A08 = A[8]; A09 = A[9]; OPERATION[1:0] = ALUOperation[1:0];
  //   Binvert = ALUOperation[2]; Ainvert = ALUOperation[3]; B00 = B[0]; B01 = B[1]; B02 = B[2]; B03 = B[3];
  //   B04 = B[4]; B05 = B[5]; B06 = B[6]; B07 = B[7]; B08 = B[8]; B09 = B[9]; R1 = out_5[0]; R2 = out_5[1];
  //   R3 = out_5[2]; R4 = out_5[3]; R5 = out_5[4]; R6 = out_5[5]; R7 = out_5[6]; R8 = out_5[7]; R9 = out_5[8];
  //   R10 = out_5[9]; R11 = out_5[10]; R12 = out_5[11]; R13 = out_5[12]; R14 = out_5[13]; R15 = out_5[14];
  //   R16 = out_5[15]; R17 = out_5[16]; R18 = out_5[17]; R19 = out_5[18]; R20 = out_5[19]; R21 = out_5[20];
  //   R22 = out_5[21]; R23 = out_5[22]; R24 = out_5[23]; R25 = out_5[24]; R26 = out_5[25]; R27 = out_5[26];
  //   R28 = out_5[27]; R29 = out_5[28]; R30 = out_5[29]; R31 = out_5[30]; R32 = out_5[31]
endmodule

module ALU1MSB (
  input  Ainvert,
  input  A,
  input  B,
  input  Less,
  input  Binvert,
  input  Cin,
  input  [1:0] Operation,
  output Result,
  output Cout,
  output Set
);

  wire and_1_out, fulladder_1_s, multiplexer_1_out, multiplexer_2_out, not_1_out, not_2_out, or_1_out,
       xor_1_out;

  not not_1 (not_1_out, A);
  not not_2 (not_2_out, B);
  Multiplexer multiplexer_1 (.in0(A), .in1(not_1_out), .out(multiplexer_1_out), .sel(Ainvert));
  Multiplexer multiplexer_2 (.in0(B), .in1(not_2_out), .out(multiplexer_2_out), .sel(Binvert));
  and and_1 (and_1_out, multiplexer_1_out, multiplexer_2_out);
  or or_1 (or_1_out, multiplexer_1_out, multiplexer_2_out);
  FullAdder fulladder_1 (.A(multiplexer_1_out), .B(multiplexer_2_out), .Cin(Cin), .S(fulladder_1_s), .Cout(Cout));
  Multiplexer #(.select(2)) multiplexer_3 (
    .in0(and_1_out), .in1(or_1_out), .in2(fulladder_1_s), .in3(Less), .out(Result), .sel(Operation));
  xor xor_1 (xor_1_out, Cout, Cin);
  xor xor_2 (Set, fulladder_1_s, xor_1_out);
endmodule

module fetch (
  input  [31:0] nextPC,
  input  CLK,
  input  reset,
  output [31:0] PCplus4,
  output [31:0] Instruction
);

  wire [31:0] PC_q;

  Register #(.width(32), .trigger("rising")) PC (.D(nextPC), .en(1'b1), .Q(PC_q), .clk(CLK), .clr(reset));
  Adder #(.width(32)) Sumador_PC4 (.a(PC_q), .b(32'h4), .out(PCplus4), .cin(1'b0));  // open: cout
  ROM #(.addrWidth(8), .dataWidth(32)) ROM_256_x_32 (.addr(PC_q[9:2]), .data(Instruction));

  // Notes on the sheet:
  //   contents of ROM_256_x_32 (hex, n*v repeats v):
  //   20080200 2009020a ad090000 81040000 20050100 c000012 20060300 acc20000 20050100 c000036 acc20004
  //   acc30008 8cd30000 8cd40004 8cd50008 20080120 8d160004 8000011 23bdfff4 afbf0008 afb10004 afb20000
  //   20110000 20120001 20080000 a05820 104482a 11200014 1100000a 200a0001 110a000c 2525020 1515020
  //   2408820 1409020 ad6a0000 216b0004 21080001 800001a ad600000 216b0004 21080001 800001a 200a0001
  //   ad6a0000 216b0004 21080001 800001a 2401020 8fbf0008 8fb10004 8fb20000 23bd000c 3e00008 23bdfffc
  //   afbf0000 20020000 20030000 20080000 a05820 104482a 11200006 816a0000 4a1020 20630001 216b0004
  //   21080001 800003c 8fbf0000 23bd0004 3e00008 185*0
endmodule
