// Logisim project procesador_monociclo.circ as structural Verilog: 8 circuits, main circuit main
module alu32 (
  input  [31:0] A,
  input  [31:0] B,
  input  [2:0] OP,
  output [31:0] R,
  output Z
);

  wire comparator_1_lt;
  wire [31:0] adder_1_out, and_1_out, bit_extender_1_out, nor_1_out, or_1_out, subtractor_1_out;

  assign and_1_out = A & B;  // AND_Gate and_1, 32 bits wide
  assign or_1_out = A | B;  // OR_Gate or_1, 32 bits wide
  assign nor_1_out = ~(A | B);  // NOR_Gate nor_1, 32 bits wide
  Adder #(.width(32)) adder_1 (.a(A), .b(B), .out(adder_1_out));  // open: cin, cout
  Subtractor #(.width(32)) subtractor_1 (.a(A), .b(B), .out(subtractor_1_out));  // open: bin, bout
  Comparator #(.width(32), .mode("twosComplement")) comparator_1 (.a(A), .b(B), .lt(comparator_1_lt));  // open: gt, eq
  assign bit_extender_1_out = {{31{1'b0}}, comparator_1_lt};  // Bit_Extender bit_extender_1
  Multiplexer #(.select(3), .width(32)) multiplexer_1 (
    .in0(adder_1_out), .in1(subtractor_1_out), .in2(and_1_out), .in3(or_1_out), .in4(nor_1_out),
    .in5(bit_extender_1_out), .in6({32{1'b0}}), .in7({32{1'b0}}), .out(R), .sel(OP));
  Comparator #(.width(32), .mode("unsigned")) comparator_2 (.a(R), .b({32{1'b0}}), .eq(Z));  // open: gt, lt
endmodule

module banco_registros (
  input  [4:0] rs,
  input  [4:0] rt,
  input  [4:0] wr,
  input  [31:0] wd,
  input  we,
  input  clk,
  input  rst,
  output [31:0] A,
  output [31:0] B,
  output [31:0] R0,
  output [31:0] R1,
  output [31:0] R2,
  output [31:0] R3,
  output [31:0] R4,
  output [31:0] R5,
  output [31:0] R6,
  output [31:0] R7,
  output [31:0] R8,
  output [31:0] R9,
  output [31:0] R10,
  output [31:0] R11,
  output [31:0] R12,
  output [31:0] R13,
  output [31:0] R14,
  output [31:0] R15,
  output [31:0] R16,
  output [31:0] R17,
  output [31:0] R18,
  output [31:0] R19,
  output [31:0] R20,
  output [31:0] R21,
  output [31:0] R22,
  output [31:0] R23,
  output [31:0] R24,
  output [31:0] R25,
  output [31:0] R26,
  output [31:0] R27,
  output [31:0] R28,
  output [31:0] R29,
  output [31:0] R30,
  output [31:0] R31
);

  wire Decodificador_out1, Decodificador_out2, Decodificador_out3, Decodificador_out4, Decodificador_out5,
       Decodificador_out6, Decodificador_out7, Decodificador_out8, Decodificador_out9, Decodificador_out10,
       Decodificador_out11, Decodificador_out12, Decodificador_out13, Decodificador_out14,
       Decodificador_out15, Decodificador_out16, Decodificador_out17, Decodificador_out18,
       Decodificador_out19, Decodificador_out20, Decodificador_out21, Decodificador_out22,
       Decodificador_out23, Decodificador_out24, Decodificador_out25, Decodificador_out26,
       Decodificador_out27, Decodificador_out28, Decodificador_out29, Decodificador_out30,
       Decodificador_out31, undriven, undriven_2, undriven_3, undriven_4, undriven_5, undriven_6, undriven_7,
       undriven_8, undriven_9, undriven_10, undriven_11, undriven_12, undriven_13, undriven_14, undriven_15,
       undriven_16, undriven_17, undriven_18, undriven_19, undriven_20, undriven_21, undriven_22,
       undriven_23, undriven_24, undriven_25, undriven_26, undriven_27, undriven_28, undriven_29,
       undriven_30, undriven_31, undriven_32, undriven_33, undriven_34, undriven_35, undriven_36,
       undriven_37, undriven_38, undriven_39, undriven_40, undriven_41, undriven_42, undriven_43,
       undriven_44, undriven_45, undriven_46, undriven_47, undriven_48, undriven_49, undriven_50,
       undriven_51, undriven_52, undriven_53, undriven_54, undriven_55, undriven_56, undriven_57,
       undriven_58, undriven_59, undriven_60, undriven_61, undriven_62, undriven_63;
  wire [31:0] registro0_q, registro1_q, registro2_q, registro3_q, registro4_q, registro5_q, registro6_q,
       registro7_q, registro8_q, registro9_q, registro11_q, registro12_q, registro13_q, registro14_q,
       registro15_q, registro16_q, registro17_q, registro18_q, registro19_q, registro20_q, registro21_q,
       registro22_q, undriven_64, undriven_65, undriven_66, undriven_67, undriven_68, undriven_69,
       undriven_70, undriven_71, undriven_72, undriven_73, undriven_74, undriven_75, undriven_76,
       undriven_77, undriven_78, undriven_79, undriven_80, undriven_81, undriven_82, undriven_83,
       undriven_84, undriven_85, undriven_86, undriven_87, undriven_88, undriven_89, undriven_90,
       undriven_91, undriven_92, undriven_93, undriven_94, undriven_95, undriven_96, undriven_97,
       undriven_98, undriven_99, undriven_100, undriven_101, undriven_102, undriven_103, undriven_104,
       undriven_105, undriven_106, undriven_107, undriven_108, undriven_109, undriven_110, undriven_111,
       undriven_112, undriven_113, undriven_114, undriven_115, undriven_116, undriven_117, undriven_118,
       undriven_119, undriven_120, undriven_121, undriven_122, undriven_123, undriven_124, undriven_125,
       undriven_126, undriven_127, undriven_128, undriven_129, undriven_130, undriven_131, undriven_132,
       undriven_133, undriven_134;

  Decoder #(.select(5), .enable("true")) Decodificador (
    .out1(Decodificador_out1), .out2(Decodificador_out2), .out3(Decodificador_out3),
    .out4(Decodificador_out4), .out5(Decodificador_out5), .out6(Decodificador_out6),
    .out7(Decodificador_out7), .out8(Decodificador_out8), .out9(Decodificador_out9),
    .out10(Decodificador_out10), .out11(Decodificador_out11), .out12(Decodificador_out12),
    .out13(Decodificador_out13), .out14(Decodificador_out14), .out15(Decodificador_out15),
    .out16(Decodificador_out16), .out17(Decodificador_out17), .out18(Decodificador_out18),
    .out19(Decodificador_out19), .out20(Decodificador_out20), .out21(Decodificador_out21),
    .out22(Decodificador_out22), .out23(Decodificador_out23), .out24(Decodificador_out24),
    .out25(Decodificador_out25), .out26(Decodificador_out26), .out27(Decodificador_out27),
    .out28(Decodificador_out28), .out29(Decodificador_out29), .out30(Decodificador_out30),
    .out31(Decodificador_out31), .sel(wr), .en(we));  // open: out0
  Register #(.width(32), .trigger("rising")) registro0 (
    .D({32{1'b0}}), .en(1'b1), .Q(registro0_q), .clk(undriven_33), .clr(undriven_2));
  Register #(.width(32), .trigger("rising")) registro1 (
    .D(undriven_64), .en(Decodificador_out1), .Q(registro1_q), .clk(undriven_34), .clr(undriven_3));
  Register #(.width(32), .trigger("rising")) registro2 (
    .D(undriven_65), .en(Decodificador_out2), .Q(registro2_q), .clk(undriven_35), .clr(undriven_4));
  Register #(.width(32), .trigger("rising")) registro3 (
    .D(undriven_66), .en(Decodificador_out3), .Q(registro3_q), .clk(undriven_36), .clr(undriven_5));
  Register #(.width(32), .trigger("rising")) registro4 (
    .D(undriven_67), .en(Decodificador_out4), .Q(registro4_q), .clk(undriven_37), .clr(undriven_6));
  Register #(.width(32), .trigger("rising")) registro5 (
    .D(undriven_68), .en(Decodificador_out5), .Q(registro5_q), .clk(undriven_38), .clr(undriven_7));
  Register #(.width(32), .trigger("rising")) registro6 (
    .D(undriven_69), .en(Decodificador_out6), .Q(registro6_q), .clk(undriven_39), .clr(undriven_8));
  Register #(.width(32), .trigger("rising")) registro7 (
    .D(undriven_70), .en(Decodificador_out7), .Q(registro7_q), .clk(undriven_40), .clr(undriven_9));
  Register #(.width(32), .trigger("rising")) registro8 (
    .D(undriven_71), .en(Decodificador_out8), .Q(registro8_q), .clk(undriven_41), .clr(undriven_10));
  Register #(.width(32), .trigger("rising")) registro9 (
    .D(undriven_72), .en(Decodificador_out9), .Q(registro9_q), .clk(undriven_42), .clr(undriven_11));
  Register #(.width(32), .trigger("rising")) registro10 (
    .D(undriven_73), .en(Decodificador_out10), .Q(R10), .clk(undriven_43), .clr(undriven_12));
  Register #(.width(32), .trigger("rising")) registro11 (
    .D(undriven_74), .en(Decodificador_out11), .Q(registro11_q), .clk(undriven_44), .clr(undriven_13));
  Register #(.width(32), .trigger("rising")) registro12 (
    .D(undriven_75), .en(Decodificador_out12), .Q(registro12_q), .clk(undriven_45), .clr(undriven_14));
  Register #(.width(32), .trigger("rising")) registro13 (
    .D(undriven_76), .en(Decodificador_out13), .Q(registro13_q), .clk(undriven_46), .clr(undriven_15));
  Register #(.width(32), .trigger("rising")) registro14 (
    .D(undriven_77), .en(Decodificador_out14), .Q(registro14_q), .clk(undriven_47), .clr(undriven_16));
  Register #(.width(32), .trigger("rising")) registro15 (
    .D(undriven_78), .en(Decodificador_out15), .Q(registro15_q), .clk(undriven_48), .clr(undriven_17));
  Register #(.width(32), .trigger("rising")) registro16 (
    .D(undriven_79), .en(Decodificador_out16), .Q(registro16_q), .clk(undriven_49), .clr(undriven_18));
  Register #(.width(32), .trigger("rising")) registro17 (
    .D(undriven_80), .en(Decodificador_out17), .Q(registro17_q), .clk(undriven_50), .clr(undriven_19));
  Register #(.width(32), .trigger("rising")) registro18 (
    .D(undriven_81), .en(Decodificador_out18), .Q(registro18_q), .clk(undriven_51), .clr(undriven_20));
  Register #(.width(32), .trigger("rising")) registro19 (
    .D(undriven_82), .en(Decodificador_out19), .Q(registro19_q), .clk(undriven_52), .clr(undriven_21));
  Register #(.width(32), .trigger("rising")) registro20 (
    .D(undriven_83), .en(Decodificador_out20), .Q(registro20_q), .clk(undriven_53), .clr(undriven_22));
  Register #(.width(32), .trigger("rising")) registro21 (
    .D(undriven_84), .en(Decodificador_out21), .Q(registro21_q), .clk(undriven_54), .clr(undriven_23));
  Register #(.width(32), .trigger("rising")) registro22 (
    .D(undriven_85), .en(Decodificador_out22), .Q(registro22_q), .clk(undriven_55), .clr(undriven_24));
  Register #(.width(32), .trigger("rising")) registro23 (
    .D(undriven_86), .en(Decodificador_out23), .Q(R23), .clk(undriven_56), .clr(undriven_25));
  Register #(.width(32), .trigger("rising")) registro24 (
    .D(undriven_87), .en(Decodificador_out24), .Q(R24), .clk(undriven_57), .clr(undriven_26));
  Register #(.width(32), .trigger("rising")) registro25 (
    .D(undriven_88), .en(Decodificador_out25), .Q(R25), .clk(undriven_58), .clr(undriven_27));
  Register #(.width(32), .trigger("rising")) registro26 (
    .D(undriven_89), .en(Decodificador_out26), .Q(R26), .clk(undriven_59), .clr(undriven_28));
  Register #(.width(32), .trigger("rising")) registro27 (
    .D(undriven_90), .en(Decodificador_out27), .Q(R27), .clk(undriven_60), .clr(undriven_29));
  Register #(.width(32), .trigger("rising")) registro28 (
    .D(undriven_91), .en(Decodificador_out28), .Q(R28), .clk(undriven_61), .clr(undriven_30));
  Register #(.width(32), .trigger("rising")) registro29 (
    .D(undriven_92), .en(Decodificador_out29), .Q(R29), .clk(undriven_62), .clr(undriven_31));
  Register #(.width(32), .trigger("rising")) registro30 (
    .D(undriven_93), .en(Decodificador_out30), .Q(R30), .clk(undriven_63), .clr(undriven_32));
  Register #(.width(32), .trigger("rising")) registro31 (
    .D(wd), .en(Decodificador_out31), .Q(R31), .clk(undriven_33), .clr(undriven));
  Multiplexer #(.select(5), .width(32)) Mux_A_rs (
    .in0(undriven_134), .in1(undriven_133), .in2(undriven_132), .in3(undriven_131), .in4(undriven_130),
    .in5(undriven_129), .in6(undriven_128), .in7(undriven_127), .in8(undriven_126), .in9(undriven_125),
    .in10(undriven_124), .in11(undriven_123), .in12(undriven_122), .in13(undriven_119), .in14(undriven_120),
    .in15(undriven_116), .in16(undriven_115), .in17(undriven_114), .in18(undriven_113), .in19(undriven_112),
    .in20(undriven_121), .in21(undriven_111), .in22(undriven_110), .in23(undriven_104), .in24(undriven_106),
    .in25(undriven_102), .in26(undriven_117), .in27(undriven_100), .in28(undriven_98), .in29(undriven_96),
    .in30(undriven_108), .in31(undriven_94), .out(A), .sel(rs));
  Multiplexer #(.select(5), .width(32)) Mux_B_rt (
    .in0(registro0_q), .in1(registro1_q), .in2(registro2_q), .in3(registro3_q), .in4(registro4_q),
    .in5(registro5_q), .in6(registro6_q), .in7(registro7_q), .in8(registro8_q), .in9(registro9_q),
    .in10(R10), .in11(R11), .in12(R12), .in13(R13), .in14(R14), .in15(R15), .in16(R16), .in17(R17),
    .in18(R18), .in19(R19), .in20(R20), .in21(R21), .in22(R22), .in23(undriven_105), .in24(undriven_107),
    .in25(undriven_103), .in26(undriven_118), .in27(undriven_101), .in28(undriven_99), .in29(undriven_97),
    .in30(undriven_109), .in31(undriven_95), .out(B), .sel(rt));
endmodule

module mem_instrucciones (
  input  [31:0] PC,
  output [31:0] INSTR
);

  ROM #(.addrWidth(12), .dataWidth(32)) ROM_instrucciones (.addr(PC[11:0]), .data(INSTR));

  // Notes on the sheet:
  //   contents of ROM_instrucciones (hex, n*v repeats v):
  //   20080200 0 0 0 2009020a 0 0 0 ad090000 0 0 0 81040000 0 0 0 20050100 0 0 0 c000012 0 0 0 20060300 0
  //   0 0 acc20000 0 0 0 20050100 0 0 0 c000036 0 0 0 acc20004 0 0 0 acc30008 0 0 0 8cd30000 0 0 0
  //   8cd40004 0 0 0 8cd50008 0 0 0 20080120 0 0 0 8d160004 0 0 0 8000011 0 0 0 23bdfff4 0 0 0 afbf0008 0
  //   0 0 afb10004 0 0 0 afb20000 0 0 0 20110000 0 0 0 20120001 0 0 0 20080000 0 0 0 a05820 0 0 0 104482a
  //   0 0 0 11200014 0 0 0 1100000a 0 0 0 200a0001 0 0 0 110a000c 0 0 0 2525020 0 0 0 1515020 0 0 0
  //   2408820 0 0 0 1409020 0 0 0 ad6a0000 0 0 0 216b0004 0 0 0 21080001 0 0 0 800001a 0 0 0 ad600000 0 0
  //   0 216b0004 0 0 0 21080001 0 0 0 800001a 0 0 0 200a0001 0 0 0 ad6a0000 0 0 0 216b0004 0 0 0 21080001
  //   0 0 0 800001a 0 0 0 2401020 0 0 0 8fbf0008 0 0 0 8fb10004 0 0 0 8fb20000 0 0 0 23bd000c 0 0 0
  //   3e00008 0 0 0 23bdfffc 0 0 0 afbf0000 0 0 0 20020000 0 0 0 20030000 0 0 0 20080000 0 0 0 a05820 0 0
  //   0 104482a 0 0 0 11200006 0 0 0 816a0000 0 0 0 4a1020 0 0 0 20630001 0 0 0 216b0004 0 0 0 21080001 0
  //   0 0 800003c 0 0 0 8fbf0000 0 0 0 23bd0004 0 0 0 3e00008 3815*0
endmodule

module unidad_control (
  input  [5:0] opcode,
  input  [5:0] funct,
  output RegDst,
  output ALUSrc,
  output MemtoReg0,
  output MemtoReg1,
  output RegWrite,
  output MemRead,
  output MemWrite,
  output Branch,
  output Jump,
  output Jal,
  output Jr,
  output ALUOp0,
  output ALUOp1
);

  wire [15:13] ROM_de_control_data;

  ROM #(.addrWidth(12), .dataWidth(16)) ROM_de_control (
    .addr({opcode, funct}),
    .data({ROM_de_control_data, ALUOp1, ALUOp0, Jr, Jal, Jump, Branch, MemWrite, MemRead, RegWrite, MemtoReg1, MemtoReg0, ALUSrc, RegDst}));

  // Notes on the sheet:
  //   contents of ROM_de_control (hex, n*v repeats v):
  //   8*1011 400 55*1011 64*0 64*100 64*31c 64*880 192*0 64*12 1472*0 64*3a 128*0 64*36 448*0 64*42 1280*0
endmodule

module control_alu (
  input  [1:0] ALUOp,
  input  [5:0] funct,
  output [2:0] op
);

  ROM #(.addrWidth(8), .dataWidth(3)) ROM_control_ALU (.addr({ALUOp, funct}), .data(op));

  // Notes on the sheet:
  //   contents of ROM_control_ALU (hex, n*v repeats v):
  //   64*0 64*1 34*0 1 0 2 3 0 4 0 0 5 85*0
endmodule

module mem_datos (
  input  [31:0] addr,
  input  [31:0] din,
  input  we,
  input  oe,
  input  clk,
  output [31:0] dout,
  output [31:0] lb
);

  wire [7:0] bitselector_1_out;

  RAM #(.addrWidth(12), .dataWidth(32), .enables("byte"), .databus("bibus"), .asyncread("true"), .trigger("rising"), .byteenables("NobyteEnables"), .\type ("volatile"), .clearpin("false"), .line("single"), .misaligned("false")) Memoria_de_datos (
    .addr(addr[13:2]), .we(we), .oe(oe), .clk(clk), .din(din), .dout(dout));
  BitSelector #(.width(32), .group(8)) bitselector_1 (.in(dout), .out(bitselector_1_out), .sel(addr[1:0]));
  assign lb = {{24{bitselector_1_out[7]}}, bitselector_1_out};  // Bit_Extender Extension_LB
endmodule

module proximo_pc (
  input  [31:0] pc4,
  input  [31:0] imm32,
  input  [25:0] target,
  input  [31:0] a_val,
  input  Branch,
  input  zero_flag,
  input  [1:0] pc_sel,
  output [31:0] pc_next
);

  wire Branch__Zero_out;
  wire [31:0] and_1_out, bit_extender_1_out, offset__2_out, or_1_out, PC__offset_out, secuencial__branch_out,
       shifter_1_out;

  Shifter #(.width(32), .shift("ll")) offset__2 (.in(imm32), .\dist (5'b00010), .out(offset__2_out));
  and Branch__Zero (Branch__Zero_out, Branch, zero_flag);
  assign bit_extender_1_out = {{6{1'b0}}, target};  // Bit_Extender bit_extender_1
  Adder #(.width(32)) PC__offset (.a(pc4), .b(offset__2_out), .out(PC__offset_out), .cin(1'b0));  // open: cout
  Shifter #(.width(32), .shift("ll")) shifter_1 (.in(bit_extender_1_out), .\dist (5'b00010), .out(shifter_1_out));
  Multiplexer #(.select(1), .width(32)) secuencial__branch (
    .in0(pc4), .in1(PC__offset_out), .out(secuencial__branch_out), .sel(Branch__Zero_out));
  assign and_1_out = pc4 & 32'hf0000000;  // AND_Gate and_1, 32 bits wide
  assign or_1_out = shifter_1_out | and_1_out;  // OR_Gate or_1, 32 bits wide
  Multiplexer #(.select(2), .width(32)) Proximo_PC (
    .in0(secuencial__branch_out), .in1(or_1_out), .in2(a_val), .in3(a_val), .out(pc_next), .sel(pc_sel));
endmodule

module main (
  input  RST,
  output [31:0] PC,
  output [31:0] INSTR,
  output [31:0] A,
  output [31:0] B,
  output [31:0] ALU,
  output [31:0] W,
  output [31:0] MEM,
  output [31:0] R0,
  output [31:0] R1,
  output [31:0] R2,
  output [31:0] R3,
  output [31:0] R4,
  output [31:0] R5,
  output [31:0] R6,
  output [31:0] R7,
  output [31:0] R8,
  output [31:0] R9,
  output [31:0] R10,
  output [31:0] R11,
  output [31:0] R12,
  output [31:0] R13,
  output [31:0] R14,
  output [31:0] R15,
  output [31:0] R16,
  output [31:0] R17,
  output [31:0] R18,
  output [31:0] R19,
  output [31:0] R20,
  output [31:0] R21,
  output [31:0] R22,
  output [31:0] R23,
  output [31:0] R24,
  output [31:0] R25,
  output [31:0] R26,
  output [31:0] R27,
  output [31:0] R28,
  output [31:0] R29,
  output [31:0] R30,
  output [31:0] R31
);

  wire alu32_1_z, clock_1_out, unidad_control_1_alusrc, unidad_control_1_branch, unidad_control_1_memread,
       unidad_control_1_memwrite, unidad_control_1_regwrite;
  wire [1:0] unidad_control_1_aluop0, unidad_control_1_jump, unidad_control_1_memtoreg0,
       unidad_control_1_regdst;
  wire [2:0] control_alu_1_op;
  wire [4:0] wr;
  wire [31:0] Extensor_de_signo_out, mem_datos_1_lb, Mux_ALUSrc_out, PC4_out, proximo_pc_1_pc_next;

  Clock clock_1 (.out(clock_1_out));
  Register #(.width(32), .trigger("rising")) Registro_PC (
    .D(proximo_pc_1_pc_next), .en(1'b1), .Q(PC), .clk(clock_1_out), .clr(RST));
  Adder #(.width(32)) PC4 (.a(PC), .b(32'h4), .out(PC4_out), .cin(1'b0));  // open: cout
  banco_registros banco_registros_1 (
    .rs(INSTR[25:21]), .rt(INSTR[20:16]), .wr(wr), .wd(W), .we(unidad_control_1_regwrite), .clk(clock_1_out),
    .rst(RST), .A(A), .B(B), .R0(R0), .R1(R1), .R2(R2), .R3(R3), .R4(R4), .R5(R5), .R6(R6), .R7(R7), .R8(R8),
    .R9(R9), .R10(R10), .R11(R11), .R12(R12), .R13(R13), .R14(R14), .R15(R15), .R16(R16), .R17(R17),
    .R18(R18), .R19(R19), .R20(R20), .R21(R21), .R22(R22), .R23(R23), .R24(R24), .R25(R25), .R26(R26),
    .R27(R27), .R28(R28), .R29(R29), .R30(R30), .R31(R31));
  mem_instrucciones mem_instrucciones_1 (.PC(PC), .INSTR(INSTR));
  unidad_control unidad_control_1 (
    .opcode(INSTR[31:26]), .funct(INSTR[5:0]), .RegDst(unidad_control_1_regdst[0]),
    .ALUSrc(unidad_control_1_alusrc), .MemtoReg0(unidad_control_1_memtoreg0[0]),
    .MemtoReg1(unidad_control_1_memtoreg0[1]), .RegWrite(unidad_control_1_regwrite),
    .MemRead(unidad_control_1_memread), .MemWrite(unidad_control_1_memwrite),
    .Branch(unidad_control_1_branch), .Jump(unidad_control_1_jump[0]), .Jal(unidad_control_1_regdst[1]),
    .Jr(unidad_control_1_jump[1]), .ALUOp0(unidad_control_1_aluop0[0]), .ALUOp1(unidad_control_1_aluop0[1]));
  control_alu control_alu_1 (.ALUOp(unidad_control_1_aluop0), .funct(INSTR[5:0]), .op(control_alu_1_op));
  assign Extensor_de_signo_out = {{16{INSTR[15]}}, INSTR[15:0]};  // Bit_Extender Extensor_de_signo
  Multiplexer #(.select(2), .width(5)) Registro_destino (
    .in0(INSTR[20:16]), .in1(INSTR[15:11]), .in2({5{1'b1}}), .in3({5{1'b1}}), .out(wr),
    .sel(unidad_control_1_regdst));
  Multiplexer #(.select(1), .width(32)) Mux_ALUSrc (
    .in0(B), .in1(Extensor_de_signo_out), .out(Mux_ALUSrc_out), .sel(unidad_control_1_alusrc));
  proximo_pc proximo_pc_1 (
    .pc4(PC4_out), .imm32(Extensor_de_signo_out), .target(INSTR[25:0]), .a_val(A),
    .Branch(unidad_control_1_branch), .zero_flag(alu32_1_z), .pc_sel(unidad_control_1_jump),
    .pc_next(proximo_pc_1_pc_next));
  alu32 alu32_1 (.A(A), .B(Mux_ALUSrc_out), .OP(control_alu_1_op), .R(ALU), .Z(alu32_1_z));
  mem_datos mem_datos_1 (
    .addr(ALU), .din(B), .we(unidad_control_1_memwrite), .oe(unidad_control_1_memread), .clk(clock_1_out),
    .dout(MEM), .lb(mem_datos_1_lb));
  Multiplexer #(.select(2), .width(32)) MemtoReg (
    .in0(ALU), .in1(MEM), .in2(mem_datos_1_lb), .in3(PC4_out), .out(W), .sel(unidad_control_1_memtoreg0));

  // Other names for the same wires on the sheet: a_val[31:0] = A; alu_res[31:0] = ALU; b_val[31:0] = B;
  //   rs[4:0] = INSTR[25:21]; mem_rdata[31:0] = MEM; wr_data[31:0] = W
endmodule
